# Fritzing sketch Quadruped_Robot_Schema (saved by Fritzing 0.9.3b)

parts:
  6 = Basic Servo
  2 = Basic Servo
  7 = Basic Servo
  3 = Basic Servo
  4 = Basic Servo
  8 = Basic Servo
  1 = Basic Servo
  5 = Basic Servo
  WeMos_D1_Mini1 = WeMos D1 Mini
  JP1 = Header 8 [package=1x08_smd]  # not connected
  JP2 = Header 8 [package=1x08_smd]  # not connected
  JP3 = Header 8 [package=1x08_smd]
  WeMos_D1_Mini2 = WeMos D1 Mini

nets:
  N1: 6.pulse, WeMos_D1_Mini1.D6
  N2: 2.pulse, WeMos_D1_Mini1.D1
  N3: 7.pulse, WeMos_D1_Mini1.D7
  N4: 3.pulse, WeMos_D1_Mini1.D2
  N5: 4.pulse, WeMos_D1_Mini1.D3
  N6: 8.pulse, WeMos_D1_Mini1.D8
  N7: 1.pulse, WeMos_D1_Mini1.D0
  N8: 5.pulse, WeMos_D1_Mini1.D5
  N9: JP3.1, WeMos_D1_Mini2.D5
  N10: JP3.2, WeMos_D1_Mini2.D6
  N11: JP3.3, WeMos_D1_Mini2.D7
  N12: JP3.4, WeMos_D1_Mini2.D8
  N13: JP3.5, WeMos_D1_Mini2.D3
  N14: JP3.6, WeMos_D1_Mini2.D2
  N15: JP3.7, WeMos_D1_Mini2.D1
  N16: JP3.8, WeMos_D1_Mini2.D0

notes:
  Quadruped Robot
  Fred J.  08/2019
  Servo2 - D1
  Servo3 - D2
  Servo4 - D3
  Servo5 - D5
  Servo6 - D6
  Servo7 - D7
  +
  -
  in the body
  in the leg
  Servo1 - D0
  Servo8 - D8

custom parts:
  Basic Servo: A generic servo.
